# Fritzing sketch bastiaan_etage (saved by Fritzing 0.9.3b)

parts:
  Part1 = Arduino Uno (Rev3)
  LED1 = LED - 5mm [color="Red (633nm)" package="5 mm [THT]"]  # not connected
  R1 = Resistor [tolerance=±5% resistance=220 package=THT]
  S1 = Pushbutton [package="[THT]"]
  LED2 = LED - 5mm [color="White (4500K)" package="5 mm [THT]"]  # not connected
  LED3 = LED - 5mm [color="Red (633nm)" package="5 mm [THT]"]  # not connected
  S2 = Pushbutton [package="[THT]"]
  R2 = Resistor [tolerance=±5% resistance=220 package=THT]
  R3 = Resistor [tolerance=±5% resistance=220 package=THT]
  R4 = Resistor [tolerance=±5% resistance=220 package=THT]
  DI1 = 7-Segment LED Display [package=THT]
  S3 = SWITCH-MOMENTARY-2 [package=reed_switch_pth]

nets:
  N1: Part1.D8, DI1.cathodeG
  N2: Part1.D9_PWM, R1.Pin_1
  N3: Part1.D10_PWM/SS, S1.Pin_1, S1.Pin_2
  N4: Part1.D11_PWM/MOSI, R2.Pin_1
  N5: Part1.D12/MISO, S2.Pin_1, S2.Pin_2
  N6: Part1.D13/SCK, R3.Pin_1
  N7: Part1.D2, DI1.cathodeA
  N8: Part1.D3_PWM, DI1.cathodeB
  N9: Part1.D4, DI1.cathodeC
  N10: Part1.D5_PWM, DI1.cathodeD
  N11: Part1.D6_PWM, DI1.cathodeE
  N12: Part1.D7, DI1.cathodeF
  N13: R4.Pin_1, S3.1

notes:
  Bastiaans etage
  5V, GRD, Data en Clock gaan weer naar de volgende etage
  5V, GRD, Data en Clock komen door van de vorige etage
